# Fritzing sketch crop protection ciecuit (saved by Fritzing 0.9.10b)

parts:
  Part1 = Arduino Uno (Rev3)
  M1 = Dagu DGServo 9g (Top view) [part_number=RS001B]
  YL-83_-_Detection_Board1 = YL-83 Rain Sensor - Detection Board
  YL-83_-_Control_Board1 = YL-83 Rain Sensor - Control Board

nets:
  N1: Part1.A0, YL-83_-_Control_Board1.AO
  N2: Part1.D3_PWM, M1.pulse
  5V: Part1.5V, YL-83_-_Control_Board1.VCC
  GND: Part1.GND, M1.gnd, YL-83_-_Control_Board1.GND
  N3: YL-83_-_Detection_Board1.POS, YL-83_-_Control_Board1.POS
  N4: YL-83_-_Detection_Board1.NEG, YL-83_-_Control_Board1.NEG

custom parts:
  YL-83 Rain Sensor - Detection Board: The YL-83 is a rain sensor that has more resistance when dry and less resistance when wet. The module runs at 5V.
  YL-83 Rain Sensor - Control Board: The YL-83 is a rain sensor that has more resistance when dry and less resistance when wet. The module runs at 5V.
